# Fritzing sketch hardware (saved by Fritzing 0.5.2b)
breadboards: 1

parts:
  Arduino1 = Arduino Nano v2.3
  R1 = Resistor [resistance=100k package=THT]
  R1_2 = Resistor [resistance=100k package=THT]
  R2 = Resistor [resistance=10k package=THT]
  R2_2 = Resistor [resistance=10k package=THT]
  J1 = female pin header, 8 pins [form="♀ (female)"]

nets:
  N1: Arduino1.GND, R1.Pin_1, R1_2.Pin_1, J1.pin4, J1.pin5
  N2: Arduino1.D2, R2.Pin_1, J1.pin2
  N3: Arduino1.D3, R2_2.Pin_1, J1.pin7
  N4: Arduino1.A1, R1_2.Pin_0, J1.pin6
  N5: Arduino1.A0, R1.Pin_0, J1.pin3
  N6: Arduino1.+5V, R2.Pin_0, R2_2.Pin_0, J1.pin8
